// Logisim project project3.circ as structural Verilog: 6 circuits, main circuit main2
module main2 (
  input  first_select_bit,
  input  second_select_bit,
  input  minus_ve_sign_A,
  input  minus_ve_sign_B,
  input  A0,
  input  A1,
  input  B0,
  input  B1,
  output div_by_zero,
  output minus_ve_sign_result,
  output zero
);

  wire and_2_out, main_1_p8, main_1_p9, main_1_p10, main_1_p11, multiplexer_1_out, multiplexer_2_out,
       multiplexer_3_out, multiplexer_4_out, n7448_1_p10, n7448_1_p11, n7448_1_p12, n7448_1_p13, n7448_1_p14,
       n7448_1_p15, n7448_1_p16, n7448_2_p9, not_1_out, or_1_out, pro_mult_1_c0, pro_mult_1_c1,
       pro_mult_1_c2, pro_mult_1_c3, pro_mult_1_minus_ve_sign, pro_reminder_1_c0, pro_reminder_1_c1,
       pro_reminder_1_div_by_zero, pro_reminder_1_final_sign;

  // amr3_main main_1: pin names not known; wires that end beside it: first_select_bit, minus_ve_sign_A, minus_ve_sign_B, A0, A1, B0, B1, main_1_p8, main_1_p9, main_1_p10, main_1_p11
  pro_mult pro_mult_1 (
    .minus_ve_sign_first(minus_ve_sign_A), .minus_ve_sign_second(minus_ve_sign_B), .A0(A0), .A1(A1), .B0(B0),
    .B1(B1), .minus_ve_sign(pro_mult_1_minus_ve_sign), .C0(pro_mult_1_c0), .C1(pro_mult_1_c1),
    .C2(pro_mult_1_c2), .C3(pro_mult_1_c3));
  pro_reminder pro_reminder_1 (
    .minus_ve_sign_A(minus_ve_sign_A), .minus_ve_sign_B(minus_ve_sign_B), .A0(A0), .A1(A1), .B0(B0), .B1(B1),
    .div_by_zero(pro_reminder_1_div_by_zero), .final_sign(pro_reminder_1_final_sign), .C0(pro_reminder_1_c0),
    .C1(pro_reminder_1_c1));
  not not_1 (not_1_out, first_select_bit);
  and and_1 (div_by_zero, first_select_bit, pro_reminder_1_div_by_zero, second_select_bit);
  and and_2 (and_2_out, pro_mult_1_c3, second_select_bit, not_1_out);
  Multiplexer #(.select(2)) multiplexer_1 (
    .in0(main_1_p9), .in1(main_1_p9), .in2(pro_mult_1_c0), .in3(pro_reminder_1_c0), .out(multiplexer_1_out),
    .sel({second_select_bit, first_select_bit}));  // open: en
  Multiplexer #(.select(2)) multiplexer_2 (
    .in0(main_1_p8), .in1(main_1_p8), .in2(pro_mult_1_minus_ve_sign), .in3(pro_reminder_1_final_sign),
    .out(multiplexer_2_out), .sel({second_select_bit, first_select_bit}));  // open: en
  Multiplexer #(.select(2)) multiplexer_3 (
    .in0(main_1_p10), .in1(main_1_p10), .in2(pro_mult_1_c1), .in3(pro_reminder_1_c1),
    .out(multiplexer_3_out), .sel({second_select_bit, first_select_bit}));  // open: en
  Multiplexer #(.select(2)) multiplexer_4 (
    .in0(main_1_p11), .in1(main_1_p11), .in2(pro_mult_1_c2), .in3(1'b0), .out(multiplexer_4_out),
    .sel({second_select_bit, first_select_bit}));  // open: en
  or or_1 (or_1_out, multiplexer_1_out, multiplexer_3_out, multiplexer_4_out, and_2_out);
  and and_3 (minus_ve_sign_result, multiplexer_2_out, or_1_out);
  not not_2 (zero, or_1_out);
  // _7448 7448_1: pin names not known; wires that end beside it: multiplexer_3_out, multiplexer_4_out, 1'b1, 1'b1, 1'b1, and_2_out, multiplexer_1_out, 1'b0, 1'b1, n7448_1_p10, n7448_1_p11, n7448_1_p12, n7448_1_p13, n7448_1_p14, n7448_1_p15, n7448_1_p16
  // _7448 7448_2: pin names not known; wires that end beside it: minus_ve_sign_result, 1'b0, 1'b1, 1'b1, 1'b1, 1'b0, 1'b0, 1'b0, n7448_2_p9
  _7_Segment_Display u_7_segment_display_1 (.g(n7448_2_p9));  // open: f, a, b, e, d, c, dp
  _7_Segment_Display u_7_segment_display_2 (
    .g(n7448_1_p11), .f(n7448_1_p10), .a(n7448_1_p12), .b(n7448_1_p13), .e(n7448_1_p16), .d(n7448_1_p15),
    .c(n7448_1_p14), .dp(1'b0));
endmodule

module half_adder (
  input  in_1,
  input  in_2,
  output out_3,
  output out_4
);

  xor xor_1 (out_3, in_1, in_2);
  and and_1 (out_4, in_1, in_2);
endmodule

module full_adder (
  input  in_1,
  input  in_2,
  input  in_3,
  output out_4,
  output out_5
);

  wire half_adder_1_out_3, half_adder_1_out_4, half_adder_2_out_4;

  half_adder half_adder_1 (.in_1(in_1), .in_2(in_3), .out_3(half_adder_1_out_3), .out_4(half_adder_1_out_4));
  half_adder half_adder_2 (.in_1(half_adder_1_out_3), .in_2(in_2), .out_3(out_4), .out_4(half_adder_2_out_4));
  or or_1 (out_5, half_adder_2_out_4, half_adder_1_out_4);
endmodule

module adder_sub (
  input  Operation,
  input  Sign_A,
  input  in_3,
  input  A0,
  input  A1,
  input  B0,
  input  B1,
  output Sign,
  output S0,
  output S1,
  output S3
);

  wire and_1_out, and_2_out, and_4_out, and_5_out, and_6_out, and_7_out, full_adder_1_p5, full_adder_2_p4,
       full_adder_2_p5, not_1_out, not_2_out, not_3_out, not_4_out, not_5_out, not_6_out, or_1_out, or_2_out,
       xor_1_out, xor_2_out, xor_3_out, xor_4_out, xor_5_out, xor_6_out;

  xor xor_1 (xor_1_out, Operation, in_3);
  xor xor_2 (xor_2_out, Sign_A, xor_1_out);
  and and_1 (and_1_out, xor_2_out, xor_1_out);
  and and_2 (and_2_out, Sign_A, xor_2_out);
  xor xor_3 (xor_3_out, and_1_out, B0);
  xor xor_4 (xor_4_out, and_1_out, B1);
  xor xor_5 (xor_5_out, and_2_out, A0);
  xor xor_6 (xor_6_out, and_2_out, A1);
  // full_adder_part full_adder_1: pin names not known; wires that end beside it: xor_5_out, xor_3_out, xor_2_out, S0, full_adder_1_p5
  // full_adder_part full_adder_2: pin names not known; wires that end beside it: xor_6_out, xor_4_out, full_adder_1_p5, full_adder_2_p4, full_adder_2_p5
  not not_1 (not_1_out, full_adder_2_p5);
  not not_2 (not_2_out, S0);
  not not_3 (not_3_out, xor_2_out);
  and and_3 (S3, not_3_out, full_adder_2_p5);
  and and_4 (and_4_out, xor_2_out, not_1_out);
  or or_1 (or_1_out, not_2_out, full_adder_2_p5);
  and and_5 (and_5_out, Sign_A, xor_1_out);
  not not_4 (not_4_out, xor_2_out);
  or or_2 (or_2_out, not_4_out, or_1_out);
  or or_3 (Sign, and_4_out, and_5_out);
  not not_5 (not_5_out, full_adder_2_p4);
  not not_6 (not_6_out, full_adder_2_p5);
  and and_6 (and_6_out, or_2_out, full_adder_2_p4);
  and and_7 (and_7_out, S0, not_5_out, xor_2_out, not_6_out);
  or or_4 (S1, and_7_out, and_6_out);

  // Notes on the sheet:
  //   Sign B
endmodule

module pro_mult (
  input  minus_ve_sign_first,
  input  minus_ve_sign_second,
  input  A0,
  input  A1,
  input  B0,
  input  B1,
  output minus_ve_sign,
  output C0,
  output C1,
  output C2,
  output C3
);

  wire and_2_out, and_3_out, and_4_out, half_adder_1_out_4;

  xor xor_1 (minus_ve_sign, minus_ve_sign_first, minus_ve_sign_second);
  and and_1 (C0, A0, B0);
  and and_2 (and_2_out, A1, B0);
  and and_3 (and_3_out, A0, B1);
  half_adder half_adder_1 (.in_1(and_2_out), .in_2(and_3_out), .out_3(C1), .out_4(half_adder_1_out_4));
  and and_4 (and_4_out, B1, A1);
  half_adder half_adder_2 (.in_1(half_adder_1_out_4), .in_2(and_4_out), .out_3(C2), .out_4(C3));
endmodule

module pro_reminder (
  input  minus_ve_sign_A,
  input  minus_ve_sign_B,
  input  A0,
  input  A1,
  input  B0,
  input  B1,
  output div_by_zero,
  output final_sign,
  output C0,
  output C1
);

  wire and_1_out, not_1_out, not_2_out, not_3_out, not_4_out;

  and and_1 (and_1_out, A1, B0);
  not not_1 (not_1_out, B0);
  not not_2 (not_2_out, B1);
  not not_3 (not_3_out, and_1_out);
  and and_2 (div_by_zero, not_1_out, not_2_out);
  and and_3 (C0, A0, not_3_out, B1);
  not not_4 (not_4_out, A0);
  and and_4 (C1, not_4_out, A1, B1, B0);

  assign final_sign = minus_ve_sign_A;
endmodule
